// Logisim project cr8.circ as structural Verilog: 11 circuits, main circuit core
module main (
);

  wire clock_1_out, ctrl_1_dr_dev, ctrl_1_dr_f, ctrl_1_dr_io, ctrl_1_dr_k, ctrl_1_dr_lhs, ctrl_1_dr_mem,
       ctrl_1_dr_rhs, ctrl_1_dr_sel, ctrl_1_dw_sel, ctrl_1_fetch, ctrl_1_pc_inc, ctrl_1_pc_jmp,
       ctrl_1_pc_jnz, ctrl_1_sp_dec, ctrl_1_sp_inc;
  wire [1:0] ctrl_1_aw;
  wire [2:0] ctrl_1_alu_op, ctrl_1_dw;
  wire [7:0] controlled_buffer_1_out, core_1_mem_out, OP_q;

  Register OP (.D(core_1_mem_out), .en(ctrl_1_fetch), .clk(clock_1_out), .Q(OP_q), .clr(1'b0));
  byte_display byte_display_1 (.in_1(OP_q));
  assign controlled_buffer_1_out = 1'b0 ? 8'h2 : 8'bz;  // Controlled_Buffer controlled_buffer_1
  Clock clock_1 (.out(clock_1_out));
  core core_1 (
    .DW(ctrl_1_dw), .AW(ctrl_1_aw), .OP(OP_q), .CLK(clock_1_out), .DR_K(ctrl_1_dr_k), .DR_F(ctrl_1_dr_f),
    .DR_IO(ctrl_1_dr_io), .DR_MEM(ctrl_1_dr_mem), .DR_LHS(ctrl_1_dr_lhs), .DR_RHS(ctrl_1_dr_rhs),
    .DR_DEV(ctrl_1_dr_dev), .DR_SEL(ctrl_1_dr_sel), .DB_in(controlled_buffer_1_out), .DW_SEL(ctrl_1_dw_sel),
    .PC_JNZ(ctrl_1_pc_jnz), .PC_J(ctrl_1_pc_jmp), .PC_INC(ctrl_1_pc_inc), .ALU_OP(ctrl_1_alu_op),
    .SP_INC(ctrl_1_sp_inc), .SP_DEC(ctrl_1_sp_dec), .RST(1'b0), .MEM_out(core_1_mem_out));  // open: AB_in
  ctrl ctrl_1 (
    .RST(1'b0), .CLK(clock_1_out), .OP(OP_q[7:3]), .FETCH(ctrl_1_fetch), .PC_JMP(ctrl_1_pc_jmp),
    .DR_DEV(ctrl_1_dr_dev), .DR_RHS(ctrl_1_dr_rhs), .DR_LHS(ctrl_1_dr_lhs), .DR_MEM(ctrl_1_dr_mem),
    .DR_IO(ctrl_1_dr_io), .DR_F(ctrl_1_dr_f), .DR_K(ctrl_1_dr_k), .PC_JNZ(ctrl_1_pc_jnz),
    .DW_SEL(ctrl_1_dw_sel), .DR_SEL(ctrl_1_dr_sel), .SP_DEC(ctrl_1_sp_dec), .SP_INC(ctrl_1_sp_inc),
    .AW(ctrl_1_aw), .DW(ctrl_1_dw), .ALU_OP(ctrl_1_alu_op), .PC_INC(ctrl_1_pc_inc));
endmodule

module core (
  input  CLK,
  input  [7:0] DB_in,
  input  [15:0] AB_in,
  input  [2:0] DW,
  input  [1:0] AW,
  input  [7:0] OP,
  input  DR_K,
  input  DR_F,
  input  DR_IO,
  input  DR_MEM,
  input  DR_LHS,
  input  DR_RHS,
  input  DR_DEV,
  input  DR_SEL,
  input  DW_SEL,
  input  PC_JNZ,
  input  PC_J,
  input  PC_INC,
  input  [2:0] ALU_OP,
  input  SP_INC,
  input  SP_DEC,
  input  RST,
  output [7:0] MEM_out
);

  wire ALU_SEL_A, ALU_SEL_B, ALU_SEL_C, ALU_SEL_D, ALU_SEL_F, ALU_SEL_X, ALU_SEL_Y, ALU_SEL_Z, and_1_out,
       and_2_out, and_3_out, and_4_out, and_5_out, AR_PC, AW_LR, AW_PC, AW_SP, AW_XY, comparator_1_eq,
       comparator_2_eq, demultiplexer_5_out7, DR_A, DR_B, DR_C, DR_D, DR_F_t, DR_X, DR_Y, DR_Z, DW_A, DW_AF,
       DW_ALU, DW_B, DW_C, DW_D, DW_DEV, DW_F, DW_IO, DW_K, DW_MEM, DW_OP, DW_RHS, DW_X, DW_Y, DW_Z,
       not_1_out, not_2_out, not_3_out, or_3_out;
  wire [2:0] DR, DW_t;
  wire [7:0] A_q, alu_1_f, alu_1_q, ALUB, B_q, C_q, controlled_buffer_19_out, controlled_buffer_26_out,
       controlled_buffer_27_out, D_q, dev_kb_1_miso, dev_rng_1_miso, F_q, IO_q, K_q, X_q, Y_q, Z_q;
  wire [7:3] LHS_q;
  wire [9:0] SP_q;
  wire [15:0] PC_q;
  wire [15:11] RHS_q;

  assign DB_in = DW_OP ? OP : 8'bz;  // Controlled_Buffer controlled_buffer_1
  Demultiplexer #(.select(3)) demultiplexer_1 (
    .out0(ALU_SEL_A), .out1(ALU_SEL_B), .out2(ALU_SEL_C), .out3(ALU_SEL_D), .out4(ALU_SEL_X),
    .out5(ALU_SEL_Y), .out6(ALU_SEL_Z), .out7(ALU_SEL_F), .in(1'b1), .sel(DR));
  Demultiplexer #(.select(3)) demultiplexer_2 (
    .out0(DW_A), .out1(DW_B), .out2(DW_C), .out3(DW_D), .out4(DW_X), .out5(DW_Y), .out6(DW_Z), .out7(DW_F),
    .in(DW_SEL), .sel(DW_t));
  Demultiplexer #(.select(2)) demultiplexer_3 (
    .out0(AW_PC), .out1(AW_SP), .out2(AW_XY), .out3(AW_LR), .in(1'b1), .sel(AW));
  not not_1 (not_1_out, DW_SEL);
  Demultiplexer #(.select(3)) demultiplexer_4 (
    .out0(DW_MEM), .out1(DW_OP), .out2(DW_ALU), .out3(DW_AF), .out4(DW_K), .out5(DW_IO), .out6(DW_DEV),
    .out7(DW_RHS), .in(not_1_out), .sel(DW));
  Demultiplexer #(.select(3)) demultiplexer_5 (
    .out0(DR_A), .out1(DR_B), .out2(DR_C), .out3(DR_D), .out4(DR_X), .out5(DR_Y), .out6(DR_Z),
    .out7(demultiplexer_5_out7), .in(DR_SEL), .sel(DR));
  or or_1 (DR_F_t, demultiplexer_5_out7, DR_F);
  Register F (.D(DB_in), .en(DR_F_t), .clk(CLK), .Q(F_q), .clr(RST));
  LED led_1 (.in(DR_F_t));
  _7_Segment_Display u_7_segment_display_1 ();  // open: g, f, a, b, e, d, c, dp
  // BCD_to_7_Segment_decoder bcd_to_7_segment_decoder_1: pin names not known
  // Binary_to_BCD_converter #(.binvalue(8)) binary_to_bcd_converter_1: pin names not known; wires that end beside it: DR_K, DB_in
  Register A (.D(DB_in), .en(DR_A), .clk(CLK), .Q(A_q), .clr(RST));
  LED led_2 (.in(DR_A));
  Register K (.D(DB_in), .en(DR_K), .clk(CLK), .Q(K_q), .clr(RST));
  LED led_3 (.in(DR_K));
  Register LHS (.D(DB_in), .en(DR_LHS), .clk(CLK), .Q({LHS_q, DR}), .clr(RST));
  LED led_4 (.in(DR_LHS));
  byte_display byte_display_1 (.in_1(F_q));
  _7_Segment_Display u_7_segment_display_2 ();  // open: g, f, a, b, e, d, c, dp
  _7_Segment_Display u_7_segment_display_3 ();  // open: g, f, a, b, e, d, c, dp
  // BCD_to_7_Segment_decoder bcd_to_7_segment_decoder_2: pin names not known
  // BCD_to_7_Segment_decoder bcd_to_7_segment_decoder_3: pin names not known
  byte_display byte_display_2 (.in_1(A_q));
  LED led_5 (.in(DW_A));
  assign DB_in = DW_A ? A_q : 8'bz;  // Controlled_Buffer controlled_buffer_2
  assign ALUB = ALU_SEL_A ? A_q : 8'bz;  // Controlled_Buffer controlled_buffer_3
  byte_display byte_display_3 (.in_1(K_q));
  LED led_6 (.in(DW_K));
  assign DB_in = DW_K ? K_q : 8'bz;  // Controlled_Buffer controlled_buffer_4
  byte_display byte_display_4 (.in_1({LHS_q, DR}));
  LED led_7 (.in(DW_F));
  assign DB_in = DW_F ? F_q : 8'bz;  // Controlled_Buffer controlled_buffer_5
  assign AB_in = AW_LR ? {RHS_q, DW_t, LHS_q, DR} : 16'bz;  // Controlled_Buffer controlled_buffer_6
  Hex_Digit_Display #(.decimalPoint("false")) hex_digit_display_1 (.value(AB_in[15:12]));
  Register B (.D(DB_in), .en(DR_B), .clk(CLK), .Q(B_q), .clr(RST));
  LED led_8 (.in(DR_B));
  Register X (.D(DB_in), .en(DR_X), .clk(CLK), .Q(X_q), .clr(RST));
  LED led_9 (.in(DR_X));
  Register RHS (.D(DB_in), .en(DR_RHS), .clk(CLK), .Q({RHS_q, DW_t}), .clr(RST));
  LED led_10 (.in(DR_RHS));
  assign DB_in = DW_ALU ? alu_1_q : 8'bz;  // Controlled_Buffer controlled_buffer_7
  Hex_Digit_Display #(.decimalPoint("false")) hex_digit_display_2 (.value(AB_in[11:8]));
  Hex_Digit_Display #(.decimalPoint("false")) hex_digit_display_3 (.value(AB_in[7:4]));
  byte_display byte_display_5 (.in_1(B_q));
  LED led_11 (.in(DW_B));
  assign DB_in = DW_B ? B_q : 8'bz;  // Controlled_Buffer controlled_buffer_8
  assign ALUB = ALU_SEL_B ? B_q : 8'bz;  // Controlled_Buffer controlled_buffer_9
  byte_display byte_display_6 (.in_1(X_q));
  LED led_12 (.in(DW_X));
  assign DB_in = DW_X ? X_q : 8'bz;  // Controlled_Buffer controlled_buffer_10
  assign ALUB = ALU_SEL_X ? X_q : 8'bz;  // Controlled_Buffer controlled_buffer_11
  assign AB_in = AW_XY ? {Y_q, X_q} : 16'bz;  // Controlled_Buffer controlled_buffer_12
  LED led_13 (.in(DW_RHS));
  byte_display byte_display_7 (.in_1({RHS_q, DW_t}));
  assign DB_in = DW_RHS ? {RHS_q, DW_t} : 8'bz;  // Controlled_Buffer controlled_buffer_13
  alu alu_1 (.B({RHS_q, DW_t}), .A(ALUB), .OP(ALU_OP), .F_in(F_q), .F(alu_1_f), .Q(alu_1_q));
  Hex_Digit_Display #(.decimalPoint("false")) hex_digit_display_4 (.value(AB_in[3:0]));
  Register C (.D(DB_in), .en(DR_C), .clk(CLK), .Q(C_q), .clr(RST));
  LED led_14 (.in(DR_C));
  Register Y (.D(DB_in), .en(DR_Y), .clk(CLK), .Q(Y_q), .clr(RST));
  LED led_15 (.in(DR_Y));
  assign DB_in = DW_AF ? alu_1_f : 8'bz;  // Controlled_Buffer controlled_buffer_14
  not not_2 (not_2_out, alu_1_f[5]);
  and and_1 (and_1_out, not_2_out, PC_JNZ);
  byte_display byte_display_8 (.in_1(C_q));
  LED led_16 (.in(DW_C));
  byte_display byte_display_9 (.in_1(Y_q));
  LED led_17 (.in(DW_Y));
  Register IO (.D(DB_in), .en(DR_IO), .clk(CLK), .Q(IO_q), .clr(RST));
  LED led_18 (.in(DR_IO));
  or or_2 (AR_PC, and_1_out, PC_J);
  assign DB_in = DW_C ? C_q : 8'bz;  // Controlled_Buffer controlled_buffer_15
  assign ALUB = ALU_SEL_C ? C_q : 8'bz;  // Controlled_Buffer controlled_buffer_16
  assign DB_in = DW_Y ? Y_q : 8'bz;  // Controlled_Buffer controlled_buffer_17
  assign ALUB = ALU_SEL_Y ? Y_q : 8'bz;  // Controlled_Buffer controlled_buffer_18
  byte_display byte_display_10 (.in_1(IO_q));
  assign controlled_buffer_19_out = and_2_out ? DB_in : 8'bz;  // Controlled_Buffer controlled_buffer_19
  Register D (.D(DB_in), .en(DR_D), .clk(CLK), .Q(D_q), .clr(RST));
  LED led_19 (.in(DR_D));
  Register Z (.D(DB_in), .en(DR_Z), .clk(CLK), .Q(Z_q), .clr(RST));
  LED led_20 (.in(DR_Z));
  LED led_21 (.in(DW_IO));
  assign DB_in = DW_IO ? IO_q : 8'bz;  // Controlled_Buffer controlled_buffer_20
  Comparator comparator_1 (.a(IO_q), .b(8'h1), .eq(comparator_1_eq));  // open: gt, lt
  and and_2 (and_2_out, DR_DEV, comparator_1_eq);
  and and_3 (and_3_out, comparator_1_eq, DW_DEV);
  byte_display byte_display_11 (.in_1(D_q));
  LED led_22 (.in(DW_D));
  assign DB_in = DW_D ? D_q : 8'bz;  // Controlled_Buffer controlled_buffer_21
  assign ALUB = ALU_SEL_D ? D_q : 8'bz;  // Controlled_Buffer controlled_buffer_22
  byte_display byte_display_12 (.in_1(Z_q));
  LED led_23 (.in(DW_Z));
  assign DB_in = DW_Z ? Z_q : 8'bz;  // Controlled_Buffer controlled_buffer_23
  assign ALUB = ALU_SEL_Z ? Z_q : 8'bz;  // Controlled_Buffer controlled_buffer_24
  assign DB_in = and_3_out ? dev_kb_1_miso : 8'bz;  // Controlled_Buffer controlled_buffer_25
  dev_kb dev_kb_1 (
    .CLK(CLK), .SEND(and_3_out), .RECV(and_2_out), .MOSI(controlled_buffer_19_out), .MISO(dev_kb_1_miso));
  assign controlled_buffer_26_out = and_4_out ? DB_in : 8'bz;  // Controlled_Buffer controlled_buffer_26
  Comparator comparator_2 (.a(IO_q), .b(8'h2), .eq(comparator_2_eq));  // open: gt, lt
  and and_4 (and_4_out, DR_DEV, comparator_2_eq);
  and and_5 (and_5_out, comparator_2_eq, DW_DEV);
  Counter #(.max('hffff), .width(16)) PC (
    .clr(RST), .load(AR_PC), .up(1'b1), .count(PC_INC), .clk(CLK), .D(AB_in), .Q(PC_q));  // open: carry
  dev_rng dev_rng_1 (
    .CLK(CLK), .SEND(and_5_out), .RECV(and_4_out), .MOSI(controlled_buffer_26_out), .MISO(dev_rng_1_miso));
  assign controlled_buffer_27_out = DR_MEM ? DB_in : 8'bz;  // Controlled_Buffer controlled_buffer_27
  assign DB_in = and_5_out ? dev_rng_1_miso : 8'bz;  // Controlled_Buffer controlled_buffer_28
  Hex_Digit_Display #(.decimalPoint("false")) hex_digit_display_5 (.value(PC_q[15:12]));
  Hex_Digit_Display #(.decimalPoint("false")) hex_digit_display_6 (.value(PC_q[11:8]));
  assign AB_in = AW_PC ? PC_q : 16'bz;  // Controlled_Buffer controlled_buffer_29
  Hex_Digit_Display #(.decimalPoint("false")) hex_digit_display_7 (.value(PC_q[7:4]));
  Hex_Digit_Display #(.decimalPoint("false")) hex_digit_display_8 (.value(PC_q[3:0]));
  mem mem_1 (.ADDR(AB_in), .WE(DR_MEM), .CLK(CLK), .D_in(controlled_buffer_27_out), .D_Out(MEM_out));
  Counter #(.max('h2ff), .width(10)) SP (
    .clr(RST), .up(not_3_out), .count(or_3_out), .clk(CLK), .D(AB_in[9:0]), .Q(SP_q));  // open: load, carry
  not not_3 (not_3_out, SP_DEC);
  or or_3 (or_3_out, SP_DEC, SP_INC);
  assign DB_in = DW_MEM ? MEM_out : 8'bz;  // Controlled_Buffer controlled_buffer_30
  Hex_Digit_Display #(.decimalPoint("false")) hex_digit_display_9 (.value(4'b1111));
  Hex_Digit_Display #(.decimalPoint("false")) hex_digit_display_10 (.value({2'b11, SP_q[9:8]}));
  Hex_Digit_Display #(.decimalPoint("false")) hex_digit_display_11 (.value(SP_q[7:4]));
  Hex_Digit_Display #(.decimalPoint("false")) hex_digit_display_12 (.value(SP_q[3:0]));
  assign AB_in = AW_SP ? {{6{1'b1}}, SP_q} : 16'bz;  // Controlled_Buffer controlled_buffer_31

  // Other names for the same wires on the sheet: AB[15:0] = AB_in; ADDRBUS_WRITER[1:0] = AW; DATABUS_WRITER[2:0] = DW;
  //   DB[7:0] = DB_in; PCJ = PC_J; PCJNZ = PC_JNZ

  // Notes on the sheet:
  //   DATA BUS
  //   ADDRESS BUS
endmodule

module ctrl (
  input  [4:0] OP,
  input  RST,
  input  CLK,
  output DR_DEV,
  output DR_RHS,
  output DR_LHS,
  output DR_MEM,
  output DR_IO,
  output DR_F,
  output DR_K,
  output PC_JNZ,
  output [1:0] AW,
  output [2:0] DW,
  output DW_SEL,
  output DR_SEL,
  output SP_DEC,
  output SP_INC,
  output [2:0] ALU_OP,
  output PC_INC,
  output PC_JMP,
  output FETCH
);

  wire [2:0] counter_1_q;
  wire [5:5] R0_data;
  wire [6:0] R2_data;

  Counter #(.max('h7), .width(3)) counter_1 (
    .clr(RST), .load(R2_data[0]), .up(1'b1), .count(1'b1), .clk(CLK), .D(3'b000), .Q(counter_1_q));  // open: carry
  Hex_Digit_Display #(.decimalPoint("false")) hex_digit_display_1 (.value({1'b0, counter_1_q}));
  ROM R0 (.addr({OP, counter_1_q}), .data({DR_K, DR_F, R0_data[5], DR_IO, DR_MEM, DR_LHS, DR_RHS, DR_DEV}));
  ROM R1 (.addr({OP, counter_1_q}), .data({DR_SEL, DW_SEL, DW, AW, PC_JNZ}));
  ROM R2 (.addr({OP, counter_1_q}), .data({PC_JMP, R2_data[6], ALU_OP, SP_INC, SP_DEC, R2_data[0]}));
  nor nor_1 (FETCH, counter_1_q[0], counter_1_q[1], counter_1_q[2]);
  or or_1 (PC_INC, R2_data[6], FETCH);

  // Notes on the sheet:
  //   contents of R0 (hex, n*v repeats v):
  //   0 4 2 6*0 4 7*0 4 2 40 5*0 4 40 4 2 12*0 4 2 6*0 10 7*0 10 4 2 2 4 0 0 0 2 8 6*0 2 10 4 2 8 0 0 0 2
  //   8 6*0 2 8 6*0 4 15*0 4 2 10 5*0 4 10 6*0 2 10 2 1 4*0 2 10 1 5*0 4 2 2 10 40 0 0 0 4 2 10 40 4*0 4 2
  //   2 10 40 0 0 0 4 2 10 40 4*0 4 2 2 40 4*0 4 2 40 5*0 4 2 2 10 40 0 0 0 4 2 10 40 4*0 4 2 2 10 40 0 0
  //   0 4 2 10 40 4*0 4 2 2 10 40 0 0 0 4 2 10 40 4*0 2 80 6*0 80
  //   contents of R1 (hex, n*v repeats v):
  //   0 8 0 c0 5*0 8 80 6*0 8 0 18 5 4*0 8 18 0 0 7 0 0 0 4 9*0 6 5*0 8 84 6*0 8 0 0 6 28 b8 0 0 8 44 6*0
  //   8 40 0 0 2e 0 0 0 8 42 6*0 8 3a 6*0 8 82 14*0 8 0 40 b0 4*0 8 0 b0 5*0 8 40 0 40 4*0 8 40 6*0 8 0 40
  //   10 18 a8 0 0 8 0 10 18 a8 0 0 0 8 0 40 10 18 a8 0 0 8 0 10 18 a8 0 0 0 8 0 40 18 4*0 8 0 18 5*0 8 0
  //   40 10 18 a8 0 0 8 0 10 18 a8 0 0 0 8 0 40 10 18 a8 0 0 8 0 10 18 a8 0 0 0 8 0 40 10 18 a8 0 0 8 0 10
  //   18 a8 0 0 0 8 40
  //   contents of R2 (hex, n*v repeats v):
  //   0 0 0 41 4*1 0 0 41 5*1 0 0 40 30 4*1 0 0 30 40 40 1 1 1 0 81 6*1 0 40 40 81 4*1 0 0 41 5*1 0 0 40
  //   40 0 0 1 1 0 0 6*1 0 0 0 40 0 41 1 1 0 0 5 5*1 0 0 5 5*1 0 2 6*1 10*0 40 0 4*1 0 0 40 5*1 0 40 0 40
  //   4*1 0 40 0 41 4*1 0 0 40 0 0 0 1 1 0 0 40 0 0 1 1 1 0 0 40 0 8 0 1 1 0 0 40 8 0 1 1 1 0 0 40 0 31 1
  //   1 1 0 0 40 31 4*1 0 0 40 0 20 0 1 1 0 0 40 20 0 1 1 1 0 0 40 0 10 0 1 1 0 0 40 10 0 1 1 1 0 0 40 0
  //   18 0 1 1 0 0 40 18 0 1 1 1 0 40 6*1 0 41 6*1
endmodule

module alu (
  input  [2:0] OP,
  input  [7:0] F_in,
  input  [7:0] A,
  input  [7:0] B,
  output [7:0] F,
  output [7:0] Q
);

  wire ad0_p1, ad1_p1, ad2_p1, and_1_out, and_3_out, and_4_out, and_5_out, and_6_out, and_7_out, and_8_out,
       and_9_out, and_10_out, and_11_out, and_12_out, and_13_out, and_14_out, and_15_out, and_16_out,
       and_18_out, and_19_out, bd0_p1, bd1_p1, bd2_p1, C, C_in, INV_B, INV_Q, not_1_out, not_2_out,
       not_3_out, not_4_out, not_5_out, or_1_out, or_3_out, or_8_out, qd0_p1, qd1_p1, qd2_p1, xor_9_out, Z;
  wire [7:0] adder_1_out, and_2_out, multiplexer_1_out, or_2_out, xor_1_out;

  xor xor_1 (xor_1_out[0], B[0], INV_B);
  xor xor_2 (xor_1_out[1], B[1], INV_B);
  xor xor_3 (xor_1_out[2], B[2], INV_B);
  xor xor_4 (xor_1_out[3], B[3], INV_B);
  xor xor_5 (xor_1_out[4], B[4], INV_B);
  xor xor_6 (xor_1_out[5], B[5], INV_B);
  xor xor_7 (xor_1_out[6], B[6], INV_B);
  xor xor_8 (xor_1_out[7], B[7], INV_B);
  or or_1 (or_1_out, OP[2], OP[1]);
  and and_1 (and_1_out, OP[1], OP[2]);
  not not_1 (not_1_out, C);
  assign or_2_out = A | xor_1_out;  // OR_Gate or_2, 8 bits wide
  assign and_2_out = A & xor_1_out;  // AND_Gate and_2, 8 bits wide
  or or_3 (or_3_out, OP[0], or_1_out);
  not not_2 (not_2_out, or_1_out);
  not not_3 (not_3_out, OP[0]);
  Adder adder_1 (.a(A), .b(xor_1_out), .out(adder_1_out), .cin(C_in), .cout(C));
  and and_3 (and_3_out, C, not_4_out);
  not not_4 (not_4_out, or_3_out);
  not not_5 (not_5_out, F_in[3]);
  and and_4 (and_4_out, OP[0], not_2_out);
  and and_5 (and_5_out, and_1_out, not_3_out);
  xor xor_9 (xor_9_out, OP[1], OP[2]);
  and and_6 (and_6_out, not_2_out, OP[0]);
  and and_7 (and_7_out, or_1_out, not_3_out);
  and and_8 (and_8_out, Z, not_2_out);
  and and_9 (and_9_out, and_1_out, F_in[4]);
  and and_10 (and_10_out, and_1_out, not_1_out);
  and and_11 (and_11_out, not_2_out, F_in[1]);
  and and_12 (and_12_out, and_1_out, Z);
  and and_13 (and_13_out, not_1_out, F_in[0]);
  Multiplexer #(.select(2), .width(8)) multiplexer_1 (
    .in0(adder_1_out), .in1(or_2_out), .in2(and_2_out), .in3(A), .out(multiplexer_1_out), .sel(OP[2:1]));
  and and_14 (and_14_out, or_3_out, F_in[2]);
  and and_15 (and_15_out, not_3_out, F_in[2]);
  and and_16 (and_16_out, OP[0], not_5_out);
  and and_17 (INV_Q, OP[0], xor_9_out);
  and and_18 (and_18_out, and_6_out, not_1_out);
  and and_19 (and_19_out, and_7_out, F_in[3]);
  or or_4 (F[4], and_8_out, and_9_out);
  LED ZF (.in(F[4]));
  or or_5 (F[1], and_10_out, and_11_out);
  LED LF (.in(F[1]));
  or or_6 (F[0], and_12_out, and_13_out);
  LED EF (.in(F[0]));
  or or_7 (F[2], and_3_out, and_14_out);
  LED CF (.in(F[2]));
  or or_8 (or_8_out, and_15_out, and_16_out);
  or or_9 (INV_B, and_4_out, and_5_out);
  LED BF (.in(F[3]));
  or or_10 (F[3], and_18_out, and_19_out);
  xor xor_10 (Q[0], multiplexer_1_out[0], INV_Q);
  xor xor_11 (Q[1], multiplexer_1_out[1], INV_Q);
  xor xor_12 (Q[2], multiplexer_1_out[2], INV_Q);
  xor xor_13 (Q[3], multiplexer_1_out[3], INV_Q);
  xor xor_14 (Q[4], multiplexer_1_out[4], INV_Q);
  xor xor_15 (Q[5], multiplexer_1_out[5], INV_Q);
  xor xor_16 (Q[6], multiplexer_1_out[6], INV_Q);
  xor xor_17 (Q[7], multiplexer_1_out[7], INV_Q);
  and and_20 (C_in, not_2_out, or_8_out);
  nor nor_1 (Z, Q[0], Q[1], Q[2], Q[3], Q[5], Q[6], Q[7], Q[4]);
  // _7_Segment_Display qd2: pin names not known; wires that end beside it: qd2_p1, qd2_p1
  // BCD_to_7_Segment_decoder bcd_to_7_segment_decoder_1: pin names not known
  // Binary_to_BCD_converter #(.binvalue(8)) binary_to_bcd_converter_1: pin names not known; wires that end beside it: Q
  // _7_Segment_Display qd1: pin names not known; wires that end beside it: qd1_p1, qd1_p1
  // BCD_to_7_Segment_decoder bcd_to_7_segment_decoder_2: pin names not known
  // _7_Segment_Display qd0: pin names not known; wires that end beside it: qd0_p1, qd0_p1
  // BCD_to_7_Segment_decoder bcd_to_7_segment_decoder_3: pin names not known
  // _7_Segment_Display ad2: pin names not known; wires that end beside it: ad2_p1, ad2_p1
  // BCD_to_7_Segment_decoder bcd_to_7_segment_decoder_4: pin names not known
  // Binary_to_BCD_converter #(.binvalue(8)) binary_to_bcd_converter_2: pin names not known; wires that end beside it: A
  // _7_Segment_Display bd2: pin names not known; wires that end beside it: bd2_p1, bd2_p1
  // BCD_to_7_Segment_decoder bcd_to_7_segment_decoder_5: pin names not known
  // Binary_to_BCD_converter #(.binvalue(8)) binary_to_bcd_converter_3: pin names not known; wires that end beside it: B
  // _7_Segment_Display ad1: pin names not known; wires that end beside it: ad1_p1, ad1_p1
  // _7_Segment_Display ad0: pin names not known; wires that end beside it: ad0_p1, ad0_p1
  // BCD_to_7_Segment_decoder bcd_to_7_segment_decoder_6: pin names not known
  // BCD_to_7_Segment_decoder bcd_to_7_segment_decoder_7: pin names not known
  // _7_Segment_Display bd1: pin names not known; wires that end beside it: bd1_p1, bd1_p1
  // _7_Segment_Display bd0: pin names not known; wires that end beside it: bd0_p1, bd0_p1
  // BCD_to_7_Segment_decoder bcd_to_7_segment_decoder_8: pin names not known
  // BCD_to_7_Segment_decoder bcd_to_7_segment_decoder_9: pin names not known

  assign F[7:5] = F_in[7:5];

  // Other names for the same wires on the sheet: P_1 = OP[1]; P_2 = OP[2]; EF = F[0]; LF = F[1]; CF = F[2]; BF = F[3];
  //   ZF = F[4]; F_E = F_in[0]; F_L = F_in[1]; F_C = F_in[2]; F_B = F_in[3]; F_Z = F_in[4]; P_0 = OP[0]
endmodule

module mem (
  input  [15:0] ADDR,
  input  WE,
  input  CLK,
  input  [7:0] D_in,
  output [7:0] D_Out
);

  wire [7:0] ram_1_dout, rom_1_data;

  RAM #(.addrWidth(15), .enables("line")) ram_1 (.addr(ADDR[14:0]), .we(WE), .clk(CLK), .din(D_in), .dout(ram_1_dout));
  ROM #(.addrWidth(15)) rom_1 (.addr(ADDR[14:0]), .data(rom_1_data));
  Multiplexer #(.width(8)) multiplexer_1 (.in0(rom_1_data), .in1(ram_1_dout), .out(D_Out), .sel(ADDR[15]));

  // Notes on the sheet:
  //   contents of rom_1 (hex, n*v repeats v):
  //   cf b 98 1 99 0 28
endmodule

module dev_kb (
  input  CLK,
  input  SEND,
  input  RECV,
  input  [7:0] MOSI,
  output [7:0] MISO
);

  wire keyboard_1_avail;

  Keyboard keyboard_1 (.clk(CLK), .re(SEND), .clr(RECV), .avail(keyboard_1_avail), .data(MISO[6:0]));
  not not_1 (MISO[7], keyboard_1_avail);
endmodule

module dev_rng (
  input  CLK,
  input  SEND,
  input  RECV,
  input  [7:0] MOSI,
  output [7:0] MISO
);

  Random random_1 (.clr(RECV), .next(SEND), .clk(CLK), .out(MISO));
endmodule

module ic (
);

  wire n74245_1_pin1, n74245_1_pin19, n74377_1_pin1, n74377_1_pin2, n74377_1_pin5, n74377_1_pin6,
       n74377_1_pin9, n74377_1_pin11, n74377_1_pin12, n74377_1_pin15, n74377_1_pin16, n74377_1_pin19;
  wire [7:0] n74377_1_pin3;

  _74377 u_74377_1 (
    .pin1(n74377_1_pin1), .pin2(n74377_1_pin2), .pin3(n74377_1_pin3[0]), .pin4(n74377_1_pin3[1]),
    .pin5(n74377_1_pin5), .pin6(n74377_1_pin6), .pin7(n74377_1_pin3[2]), .pin8(n74377_1_pin3[3]),
    .pin9(n74377_1_pin9), .pin19(n74377_1_pin19), .pin18(n74377_1_pin3[7]), .pin17(n74377_1_pin3[6]),
    .pin16(n74377_1_pin16), .pin15(n74377_1_pin15), .pin14(n74377_1_pin3[5]), .pin13(n74377_1_pin3[4]),
    .pin12(n74377_1_pin12), .pin11(n74377_1_pin11));
  _74245 u_74245_1 (
    .pin1(n74245_1_pin1), .pin2(n74377_1_pin2), .pin3(n74377_1_pin5), .pin4(n74377_1_pin6),
    .pin5(n74377_1_pin9), .pin6(n74377_1_pin12), .pin7(n74377_1_pin15), .pin8(n74377_1_pin16),
    .pin9(n74377_1_pin19), .pin19(n74245_1_pin19), .pin18(n74377_1_pin3[0]), .pin17(n74377_1_pin3[1]),
    .pin16(n74377_1_pin3[2]), .pin15(n74377_1_pin3[3]), .pin14(n74377_1_pin3[4]), .pin13(n74377_1_pin3[5]),
    .pin12(n74377_1_pin3[6]), .pin11(n74377_1_pin3[7]));
  assign n74377_1_pin3 = 1'b0 ? 8'h3 : 8'bz;  // Controlled_Buffer controlled_buffer_1
  // also tied to GND on the sheet: n74245_1_pin19
  // also tied to VCC on the sheet: {n74377_1_pin1, n74377_1_pin11, n74245_1_pin1}
endmodule

module byte_display (
  input  [7:0] in_1
);

  wire d0_p1, d1_p1, d2_p1;

  // _7_Segment_Display d2: pin names not known; wires that end beside it: d2_p1, d2_p1
  // _7_Segment_Display d1: pin names not known; wires that end beside it: d1_p1, d1_p1
  // BCD_to_7_Segment_decoder bcd_to_7_segment_decoder_1: pin names not known
  // BCD_to_7_Segment_decoder bcd_to_7_segment_decoder_2: pin names not known
  // Binary_to_BCD_converter #(.binvalue(8)) binary_to_bcd_converter_1: pin names not known; wires that end beside it: in_1
  // _7_Segment_Display d0: pin names not known; wires that end beside it: d0_p1, d0_p1
  // BCD_to_7_Segment_decoder bcd_to_7_segment_decoder_3: pin names not known
endmodule

module gfx_ctr (
  input  CLK,
  output [8:0] H,
  output hsend,
  output hsync,
  output [8:0] V,
  output vsend,
  output vsync
);

  wire and_1_out, and_2_out, and_3_out, and_4_out, and_5_out, and_6_out, and_7_out, and_8_out, and_9_out,
       and_10_out, not_1_out, not_2_out, not_3_out, not_4_out, not_5_out, not_6_out, not_7_out, not_8_out,
       not_9_out, not_10_out, not_11_out, not_12_out, not_13_out, not_14_out, not_15_out, not_16_out;

  Counter #(.max('h1ff), .width(9)) counter_1 (
    .clr(and_1_out), .load(1'b0), .up(1'b1), .count(1'b1), .clk(CLK), .Q(H));  // open: D, carry
  Counter #(.max('h1ff), .width(9)) counter_2 (
    .clr(and_2_out), .load(1'b0), .up(1'b1), .count(and_3_out), .clk(CLK), .Q(V));  // open: D, carry
  and and_1 (and_1_out, H[0], and_3_out);
  and and_2 (and_2_out, V[0], and_4_out);
  not not_1 (not_1_out, H[0]);
  not not_2 (not_2_out, H[1]);
  not not_3 (not_3_out, H[2]);
  not not_4 (not_4_out, H[3]);
  not not_5 (not_5_out, H[4]);
  not not_6 (not_6_out, H[5]);
  not not_7 (not_7_out, H[6]);
  not not_8 (not_8_out, H[7]);
  not not_9 (not_9_out, V[0]);
  not not_10 (not_10_out, V[1]);
  not not_11 (not_11_out, V[2]);
  not not_12 (not_12_out, V[3]);
  not not_13 (not_13_out, V[4]);
  not not_14 (not_14_out, V[5]);
  not not_15 (not_15_out, V[6]);
  not not_16 (not_16_out, V[7]);
  LED h264 (.in(and_3_out));
  and and_3 (and_3_out, not_2_out, not_3_out, H[3], not_5_out, not_6_out, not_7_out, not_8_out, H[8]);
  LED v264 (.in(and_4_out));
  and and_4 (and_4_out, not_10_out, not_11_out, V[3], not_13_out, not_14_out, not_15_out, not_16_out, V[8]);
  LED h242 (.in(and_5_out));
  and and_5 (and_5_out, not_1_out, H[1], not_3_out, not_4_out, H[4], H[5], H[6], H[7]);
  and and_6 (and_6_out, not_9_out, V[1], not_11_out, not_12_out, V[4], V[5], V[6], V[7]);
  LED v242 (.in(and_6_out));
  LED h210 (.in(and_7_out));
  and and_7 (and_7_out, not_1_out, H[1], not_3_out, not_4_out, H[4], not_6_out, H[6], H[7]);
  LED v210 (.in(and_8_out));
  and and_8 (and_8_out, not_9_out, V[1], not_11_out, not_12_out, V[4], not_14_out, V[6], V[7]);
  LED h200 (.in(and_9_out));
  and and_9 (and_9_out, not_1_out, not_2_out, not_3_out, H[3], not_5_out, not_6_out, H[6], H[7]);
  and and_10 (and_10_out, not_9_out, not_10_out, not_11_out, V[3], not_13_out, not_14_out, V[6], V[7]);
  S_R_Flip_Flop #(.trigger("high")) s_r_ff_1 (
    .S(and_3_out), .R(and_9_out), .clk(CLK), .Q(hsend));  // open: reset, Qn, preset
  S_R_Flip_Flop #(.trigger("high")) s_r_ff_2 (
    .S(and_5_out), .R(and_7_out), .clk(CLK), .Q(hsync));  // open: reset, Qn, preset
  LED v200 (.in(and_10_out));
  S_R_Flip_Flop s_r_ff_3 (.S(and_4_out), .R(and_10_out), .clk(CLK), .Q(vsend));  // open: reset, Qn, preset
  S_R_Flip_Flop s_r_ff_4 (.S(and_6_out), .R(and_8_out), .clk(CLK), .Q(vsync));  // open: reset, Qn, preset
endmodule

module gfx_ex (
  input  [7:0] COLOR
);

  wire and_1_out, buffer_1_out, buffer_2_out, buffer_3_out, buffer_4_out, buffer_5_out, buffer_6_out,
       clock_1_out, controlled_buffer_1_out, controlled_buffer_2_out, controlled_buffer_3_out,
       gfx_ctr_1_hsend, gfx_ctr_1_hsync, gfx_ctr_1_vsend, gfx_ctr_1_vsync, or_1_out, or_2_out, or_3_out;

  Clock clock_1 (.out(clock_1_out));
  gfx_ctr gfx_ctr_1 (
    .CLK(clock_1_out), .hsend(gfx_ctr_1_hsend), .hsync(gfx_ctr_1_hsync), .vsend(gfx_ctr_1_vsend),
    .vsync(gfx_ctr_1_vsync));  // open: H, V
  LED HSYNC (.in(gfx_ctr_1_hsync));
  LED VSYNC (.in(gfx_ctr_1_vsync));
  buf buffer_1 (buffer_1_out, COLOR[0]);
  buf buffer_2 (buffer_2_out, COLOR[1]);
  buf buffer_3 (buffer_3_out, COLOR[2]);
  buf buffer_4 (buffer_4_out, COLOR[3]);
  buf buffer_5 (buffer_5_out, COLOR[4]);
  buf buffer_6 (buffer_6_out, COLOR[5]);
  and and_1 (and_1_out, gfx_ctr_1_hsend, gfx_ctr_1_vsend);
  or or_1 (or_1_out, buffer_1_out, buffer_2_out);
  assign controlled_buffer_1_out = and_1_out ? or_1_out : 1'bz;  // Controlled_Buffer controlled_buffer_1
  or or_2 (or_2_out, buffer_3_out, buffer_4_out);
  assign controlled_buffer_2_out = and_1_out ? or_2_out : 1'bz;  // Controlled_Buffer controlled_buffer_2
  or or_3 (or_3_out, buffer_5_out, buffer_6_out);
  assign controlled_buffer_3_out = and_1_out ? or_3_out : 1'bz;  // Controlled_Buffer controlled_buffer_3
  LED R (.in(controlled_buffer_1_out));
  LED G (.in(controlled_buffer_2_out));
  LED B (.in(controlled_buffer_3_out));

  // Notes on the sheet:
  //   1.5kOhm
  //   680Ohm
  //   1.5kOhm
  //   680Ohm
  //   1.5kOhm
  //   680Ohm
  //   Active video
  //   Pretend the BUFFER gates are resisters and the OR gates are wire connections (voltage divider)
endmodule
